// Logisim project ISA.circ as structural Verilog: 4 circuits, main circuit main
module main (
);

  wire brzr, CLK, dadbReg, dadobReg, muxUla, reg1, wbreg, wm;
  wire [1:0] pcSel;
  wire [3:0] multiplexer_3_out, opcode, opUla;
  wire [11:0] adder_1_out, imm, multiplexer_1_out, multiplexer_2_out, multiplexer_4_out, multiplexer_5_out,
       PC_q, Ra, ram_1_dout, Rb, ula_1_c;
  wire [11:4] rom_1_data;

  Multiplexer #(.select(2), .width(12)) multiplexer_1 (
    .in0(adder_1_out), .in1(multiplexer_2_out), .in2(multiplexer_2_out), .out(multiplexer_1_out), .sel(pcSel));  // open: in3
  Multiplexer #(.width(12)) multiplexer_2 (.in0(adder_1_out), .out(multiplexer_2_out), .sel(brzr));  // open: in1
  Register #(.width(12)) PC (.D(multiplexer_1_out), .en(1'b1), .clk(CLK), .Q(PC_q));  // open: clr
  Clock clock_1 (.out(CLK));
  Adder #(.width(12)) adder_1 (.a(PC_q), .b(12'h1), .out(adder_1_out));  // open: cin, cout
  Adder #(.width(12)) adder_2 (.a(PC_q), .b(imm), .out(multiplexer_2_out));  // open: cin, cout
  ROM #(.addrWidth(12), .dataWidth(12)) rom_1 (.addr(PC_q), .data({rom_1_data, opcode}));
  ROM #(.addrWidth(4), .dataWidth(11)) rom_2 (.addr(opcode), .data({pcSel, reg1, wbreg, muxUla, dadobReg, wm, opUla}));
  Multiplexer #(.width(4)) multiplexer_3 (.in0(4'b0000), .in1(rom_1_data[7:4]), .out(multiplexer_3_out), .sel(reg1));
  assign imm = {{8{rom_1_data[7]}}, rom_1_data[7:4]};  // Bit_Extender bit_extender_1
  Multiplexer #(.width(12)) multiplexer_4 (.in0(ram_1_dout), .in1(ula_1_c), .out(multiplexer_4_out), .sel(dadbReg));
  bReg breg_1 (
    .D(multiplexer_4_out), .clk(CLK), .rd(rom_1_data[11:8]), .W(wbreg), .rs1(multiplexer_3_out),
    .rs2(rom_1_data[11:8]), .a(Ra), .b(Rb));
  Comparator #(.width(12)) comparator_1 (.a(Ra), .b({12{1'b0}}), .eq(brzr));  // open: gt, lt
  Multiplexer #(.width(12)) multiplexer_5 (.in0(Rb), .in1(imm), .out(multiplexer_5_out), .sel(muxUla));
  ula ula_1 (.A(Ra), .B(multiplexer_5_out), .OPULA(opUla), .C(ula_1_c));  // open: zero
  RAM #(.addrWidth(12), .dataWidth(12)) ram_1 (.addr(Rb), .we(wm), .oe(1'b1), .clk(CLK), .din(Ra), .dout(ram_1_dout));

  // Notes on the sheet:
  //   contents of rom_1 (hex, n*v repeats v):
  //   13*0 1
  //   contents of rom_2 (hex, n*v repeats v):
  //   a0 10 0 400 314 311 312 113 714 715 718 719 114 115 116 117
endmodule

module ula (
  input  [11:0] A,
  input  [11:0] B,
  input  [3:0] OPULA,
  output [11:0] C,
  output zero
);

  wire comparator_1_eq, comparator_1_gt, comparator_1_lt, multiplexer_2_out, or_1_out, or_2_out;
  wire [11:0] adder_1_out, AS, BS, divider_1_out, multiplier_1_out, shifter_1_out, shifter_2_out,
       subtractor_1_out;

  c2 c2_1 (.e(A), .s(AS));
  c2 c2_2 (.e(B), .s(BS));
  Adder #(.width(12)) adder_1 (.a(BS), .b(AS), .out(adder_1_out));  // open: cin, cout
  Subtractor #(.width(12)) subtractor_1 (.a(BS), .b(AS), .out(subtractor_1_out));  // open: bin, bout
  Divider #(.width(12)) divider_1 (.a(BS), .b(AS), .out(divider_1_out));  // open: upper, rem
  Multiplier #(.width(12)) multiplier_1 (.a(BS), .b(AS), .out(multiplier_1_out));  // open: cin, cout
  Shifter #(.shift("lr"), .width(12)) shifter_1 (.in(BS), .\dist (AS[3:0]), .out(shifter_1_out));
  Shifter #(.width(12)) shifter_2 (.in(BS), .\dist (AS[3:0]), .out(shifter_2_out));
  Comparator #(.width(12)) comparator_1 (
    .a(AS), .b(BS), .gt(comparator_1_gt), .eq(comparator_1_eq), .lt(comparator_1_lt));
  Multiplexer #(.select(4), .width(12)) multiplexer_1 (
    .in0(shifter_2_out), .in1(shifter_1_out), .in3(adder_1_out), .in4(subtractor_1_out), .in5(divider_1_out),
    .in6(multiplier_1_out), .out(C), .sel(OPULA));  // open: in2, in7, in8, in9, in10, in11, in12, in13, in14, in15
  or or_1 (or_1_out, comparator_1_gt, comparator_1_eq);
  or or_2 (or_2_out, comparator_1_lt, comparator_1_eq);
  Multiplexer #(.select(4)) multiplexer_2 (
    .in2(comparator_1_eq), .in12(comparator_1_gt), .in13(or_1_out), .in14(comparator_1_lt), .in15(or_2_out),
    .out(multiplexer_2_out), .sel(OPULA));  // open: in0, in1, in3, in4, in5, in6, in7, in8, in9, in10, in11
endmodule

module bReg (
  input  [11:0] D,
  input  clk,
  input  [3:0] rd,
  input  W,
  input  [3:0] rs1,
  input  [3:0] rs2,
  output [11:0] a,
  output [11:0] b
);

  wire demultiplexer_1_out1, demultiplexer_1_out2, demultiplexer_1_out3, demultiplexer_1_out4, mx5, mx6, mx7,
       mx8, mx9, mx10, mx11, mx12, mx13, mx14, mx15;
  wire [11:0] multiplexer_1_out, multiplexer_2_out, multiplexer_3_out, multiplexer_4_out, multiplexer_5_out,
       multiplexer_6_out, multiplexer_7_out, multiplexer_8_out, multiplexer_9_out, multiplexer_10_out,
       multiplexer_11_out, multiplexer_12_out, multiplexer_15_out, multiplexer_16_out, multiplexer_17_out,
       rs1_t, rs2_t, rs3, rs4, rs5, rs6, rs7, rs8, rs9, rs10, rs11, rs12, rs13, rs14, rs15;

  Demultiplexer #(.select(4)) demultiplexer_1 (
    .out1(demultiplexer_1_out1), .out2(demultiplexer_1_out2), .out3(demultiplexer_1_out3),
    .out4(demultiplexer_1_out4), .out5(mx5), .out6(mx6), .out7(mx7), .out8(mx8), .out9(mx9), .out10(mx10),
    .out11(mx11), .out12(mx12), .out13(mx13), .out14(mx14), .out15(mx15), .in(W), .sel(rd));  // open: out0
  Multiplexer #(.width(12)) multiplexer_1 (.in0(rs1_t), .in1(D), .out(multiplexer_1_out), .sel(demultiplexer_1_out1));
  Multiplexer #(.width(12)) multiplexer_2 (.in0(rs2_t), .in1(D), .out(multiplexer_2_out), .sel(demultiplexer_1_out2));
  Multiplexer #(.width(12)) multiplexer_3 (.in0(rs3), .in1(D), .out(multiplexer_3_out), .sel(demultiplexer_1_out3));
  Multiplexer #(.width(12)) multiplexer_4 (.in0(rs4), .in1(D), .out(multiplexer_4_out), .sel(demultiplexer_1_out4));
  Register #(.width(12)) r1 (.D(multiplexer_1_out), .clk(clk), .Q(rs1_t));  // open: en, clr
  Register #(.width(12)) r2 (.D(multiplexer_2_out), .clk(clk), .Q(rs2_t));  // open: en, clr
  Register #(.width(12)) r3 (.D(multiplexer_3_out), .clk(clk), .Q(rs3));  // open: en, clr
  Register #(.width(12)) r4 (.D(multiplexer_4_out), .clk(clk), .Q(rs4));  // open: en, clr
  Register #(.width(12)) r5 (.D(multiplexer_5_out), .clk(clk), .Q(rs5));  // open: en, clr
  Multiplexer #(.width(12)) multiplexer_5 (.in0(rs5), .in1(D), .out(multiplexer_5_out), .sel(mx5));
  Register #(.width(12)) r6 (.D(multiplexer_6_out), .clk(clk), .Q(rs6));  // open: en, clr
  Multiplexer #(.width(12)) multiplexer_6 (.in0(rs6), .in1(D), .out(multiplexer_6_out), .sel(mx6));
  Register #(.width(12)) r7 (.D(multiplexer_7_out), .clk(clk), .Q(rs7));  // open: en, clr
  Multiplexer #(.width(12)) multiplexer_7 (.in0(rs7), .in1(D), .out(multiplexer_7_out), .sel(mx7));
  Register #(.width(12)) r8 (.D(multiplexer_8_out), .clk(clk), .Q(rs8));  // open: en, clr
  Multiplexer #(.width(12)) multiplexer_8 (.in0(rs8), .out(multiplexer_8_out), .sel(mx8));  // open: in1
  Multiplexer #(.width(12)) multiplexer_9 (.in0(rs9), .in1(D), .out(multiplexer_9_out), .sel(mx9));
  Multiplexer #(.width(12)) multiplexer_10 (.in0(rs10), .in1(D), .out(multiplexer_10_out), .sel(mx10));
  Multiplexer #(.width(12)) multiplexer_11 (.in0(rs11), .in1(D), .out(multiplexer_11_out), .sel(mx11));
  Multiplexer #(.width(12)) multiplexer_12 (.in0(rs12), .out(multiplexer_12_out), .sel(mx12));  // open: in1
  Register #(.width(12)) r9 (.D(multiplexer_9_out), .clk(clk), .Q(rs9));  // open: en, clr
  Register #(.width(12)) r10 (.D(multiplexer_10_out), .clk(clk), .Q(rs10));  // open: en, clr
  Register #(.width(12)) r11 (.D(multiplexer_11_out), .clk(clk), .Q(rs11));  // open: en, clr
  Register #(.width(12)) r12 (.D(multiplexer_12_out), .clk(clk), .Q(rs12));  // open: en, clr
  Multiplexer #(.select(4), .width(12)) multiplexer_13 (
    .in0({12{1'b0}}), .in1(rs1_t), .in2(rs2_t), .in3(rs3), .in4(rs4), .in5(rs5), .in6(rs6), .in7(rs7),
    .in8(rs8), .in9(rs9), .in10(rs10), .in11(rs11), .in12(rs12), .in13(rs13), .in14(rs14), .in15(rs15),
    .out(a), .sel(rs1));
  Multiplexer #(.select(4), .width(12)) multiplexer_14 (
    .in0({12{1'b0}}), .in1(rs1_t), .in2(rs2_t), .in3(rs3), .in4(rs4), .in5(rs5), .in6(rs6), .in7(rs7),
    .in8(rs8), .in9(rs9), .in10(rs10), .in11(rs11), .in12(rs12), .in13(rs13), .in14(rs14), .in15(rs15),
    .out(b), .sel(rs2));
  Register #(.width(12)) r13 (.D(multiplexer_15_out), .clk(clk), .Q(rs13));  // open: en, clr
  Multiplexer #(.width(12)) multiplexer_15 (.in0(rs13), .in1(D), .out(multiplexer_15_out), .sel(mx13));
  Register #(.width(12)) r14 (.D(multiplexer_16_out), .clk(clk), .Q(rs14));  // open: en, clr
  Multiplexer #(.width(12)) multiplexer_16 (.in0(rs14), .in1(D), .out(multiplexer_16_out), .sel(mx14));
  Register #(.width(12)) r15 (.D(multiplexer_17_out), .clk(clk), .Q(rs15));  // open: en, clr
  Multiplexer #(.width(12)) multiplexer_17 (.in0(rs15), .in1(D), .out(multiplexer_17_out), .sel(mx15));
endmodule

module c2 (
  input  [11:0] e,
  output [11:0] s
);

  wire [11:0] not_1_out;

  not not_1 (not_1_out[0], e[0]);
  not not_2 (not_1_out[1], e[1]);
  not not_3 (not_1_out[2], e[2]);
  not not_4 (not_1_out[3], e[3]);
  not not_5 (not_1_out[4], e[4]);
  not not_6 (not_1_out[5], e[5]);
  not not_7 (not_1_out[6], e[6]);
  not not_8 (not_1_out[7], e[7]);
  not not_9 (not_1_out[8], e[8]);
  not not_10 (not_1_out[9], e[9]);
  not not_11 (not_1_out[10], e[10]);
  not not_12 (not_1_out[11], e[11]);
  Adder #(.width(12)) adder_1 (.a(not_1_out), .b(12'h1), .out(s));  // open: cin, cout
endmodule
